# Fritzing sketch Tiki Nook Control - WS2801 Pixels Only (saved by Fritzing 0.9.2b)
breadboards: 1

parts:
  +5V = 2.1mm Barrel Jack with Terminal Block
  C1 = Electrolytic Capacitor [capacitance=1000μF package="1010 [SMD, electrolytic]"]
  PCA2 = Sparkfun PCA9306 Breakout [package="DIP (Dual Inline) [THT]"]
  J1 = Cobbler Plus  # not connected
  U1 = WS2801 [package=sop-14]

nets:
  N1: +5V.POS, C1.+, PCA2.VREF2, U1.VCC
  GND: +5V.NEG, C1.-, PCA2.GND, U1.GND
  N2: PCA2.SCL2, U1.SDI
  N3: PCA2.SDA2, U1.CKI

notes:
  WS2801 chip represents strands of “12mm Diffused Thin Digital RGB LED Pixels (Strand of 25) - WS2801”
  https://www.adafruit.com/products/322
  Black — GND
  Red — +5V
  Orange — +3.3V
  Yellow — Serial Data (MOSI/SDI)
  Green — Clock (SCLK/CKI)

custom parts:
  Sparkfun PCA9306 Breakout: A stand-in part for the PCA9306 Breakout, reversed so that the pin labels appear on top of the board.
  Cobbler Plus: The Cobbler Plus is an add on prototyping board from Adafruit specifically designed for the Raspberry Pi B+ that can break out all those tasty power, GPIO, I2C and SPI pins from the 40-pin header onto a solderless breadboard. This set will make "cobbling together" prototypes with the Pi super easy. The Cobbler Plus can plug into any solderless breadboard.
