# Fritzing sketch Tiki Nook Control v01 (saved by Fritzing 0.9.2b)
breadboards: 1

parts:
  Raspberry_Pi1 = Raspberry Pi 2
  NEOPIXEL1 = Neopixel Strip -- Black (60/m)
  PCA1 = Sparkfun PCA9306 Breakout [package="DIP (Dual Inline) [THT]"]
  +5V = 2.1mm Barrel Jack with Terminal Block
  C1 = Electrolytic Capacitor [capacitance=1000μF package="1010 [SMD, electrolytic]"]
  R1 = Resistor [tolerance=±5% resistance=470 package="1206 [SMD]"]

nets:
  N1: Raspberry_Pi1.3v3, PCA1.VREF1
  N2: Raspberry_Pi1.GPIO18, PCA1.SCL1
  GND: Raspberry_Pi1.GND, NEOPIXEL1.GND, PCA1.GND, +5V.NEG, C1.-
  N3: NEOPIXEL1.+5V, PCA1.VREF2, +5V.POS, C1.+
  N4: NEOPIXEL1.DI, R1.Pin_1
  N5: PCA1.SCL2, R1.Pin_0

notes:
  SparkFun Level Translator Breakout - PCA9306
  This is an update of https://learn.adafruit.com/neopixels-on-raspberry-pi/wiring using the PCA9306 for the level shifting.

custom parts:
  Neopixel Strip -- Black (60/m): Neopixel Strip, Black, 60 pixels per meter.
  Sparkfun PCA9306 Breakout: A stand-in part for the PCA9306 Breakout, reversed so that the pin labels appear on top of the board.
