# Fritzing sketch Tiki Nook Control v02 (saved by Fritzing 0.9.2b)
breadboards: 1

parts:
  NEOPIXEL1 = Neopixel Strip -- Black (60/m)
  PCA1 = Sparkfun PCA9306 Breakout [package="DIP (Dual Inline) [THT]"]
  +5V = 2.1mm Barrel Jack with Terminal Block
  C1 = Electrolytic Capacitor [capacitance=1000μF package="1010 [SMD, electrolytic]"]
  R1 = Resistor [tolerance=±5% resistance=470 package="1206 [SMD]"]
  PCA2 = Sparkfun PCA9306 Breakout [package="DIP (Dual Inline) [THT]"]  # not connected
  J1 = Cobbler Plus  # not connected

nets:
  N1: NEOPIXEL1.+5V, PCA1.VREF2, +5V.POS, C1.+
  N2: NEOPIXEL1.DI, R1.Pin_1
  GND: NEOPIXEL1.GND, PCA1.GND, +5V.NEG, C1.-
  N3: PCA1.SCL2, R1.Pin_0

notes:
  This is an update of https://learn.adafruit.com/neopixels-on-raspberry-pi/wiring using the PCA9306 for the level shifting.

custom parts:
  Neopixel Strip -- Black (60/m): Neopixel Strip, Black, 60 pixels per meter.
  Sparkfun PCA9306 Breakout: A stand-in part for the PCA9306 Breakout, reversed so that the pin labels appear on top of the board.
  Cobbler Plus: The Cobbler Plus is an add on prototyping board from Adafruit specifically designed for the Raspberry Pi B+ that can break out all those tasty power, GPIO, I2C and SPI pins from the 40-pin header onto a solderless breadboard. This set will make "cobbling together" prototypes with the Pi super easy. The Cobbler Plus can plug into any solderless breadboard.
