# Fritzing sketch Tiki Nook Control v03 (saved by Fritzing 0.9.2b)
breadboards: 1

parts:
  Raspberry_Pi1 = Raspberry Pi 2
  NEOPIXEL1 = Neopixel Strip -- Black (60/m)
  PCA1 = Sparkfun PCA9306 Breakout [package="DIP (Dual Inline) [THT]"]
  +5V = 2.1mm Barrel Jack with Terminal Block
  C1 = Electrolytic Capacitor [capacitance=1000μF package="1010 [SMD, electrolytic]"]
  R1 = Resistor [tolerance=±5% resistance=470 package="1206 [SMD]"]
  PCA2 = Sparkfun PCA9306 Breakout [package="DIP (Dual Inline) [THT]"]
  U2 = WS2801 [package=sop-14]
  U3 = RELAY [package=relay-t9a-2]

nets:
  3V3: Raspberry_Pi1.3v3, Raspberry_Pi1.3V3, PCA1.VREF1, PCA2.VREF1
  N1: Raspberry_Pi1.GPIO4, PCA1.SDA1
  N2: Raspberry_Pi1.GPIO10, PCA2.SCL1
  N3: Raspberry_Pi1.GPIO11, PCA2.SDA1
  N4: Raspberry_Pi1.GPIO18, PCA1.SCL1
  GND: Raspberry_Pi1.GND, NEOPIXEL1.GND, PCA1.GND, +5V.NEG, C1.-, PCA2.GND, U2.GND, U3.NO
  +5V: NEOPIXEL1.+5V, PCA1.VREF2, +5V.POS, C1.+, PCA2.VREF2, U2.VCC, U3.MAIN
  N5: NEOPIXEL1.DI, R1.Pin_1
  N6: PCA1.SCL2, R1.Pin_0
  N7: PCA1.SDA2, U3.NC
  N8: PCA2.SCL2, U2.SDI
  N9: PCA2.SDA2, U2.CKI

notes:
  to smoke machine remote

custom parts:
  Neopixel Strip -- Black (60/m): Neopixel Strip, Black, 60 pixels per meter.
  Sparkfun PCA9306 Breakout: A stand-in part for the PCA9306 Breakout, reversed so that the pin labels appear on top of the board.
